// Logisim project DDA.circ as structural Verilog: 1 circuit, main circuit DDA
module DDA (
  input  MSB,
  input  i,
  input  i2,
  input  LSB,
  input  clk,
  input  rst,
  output OMSB,
  output O,
  output O1,
  output OLSB
);

  wire decoder_1_out1, decoder_1_out2, decoder_1_out3, decoder_1_out4, decoder_1_out5, decoder_1_out6,
       decoder_1_out7, decoder_1_out8, decoder_1_out9, decoder_1_out11, or_1_out, or_2_out, or_3_out,
       or_4_out;

  Decoder #(.select(4)) decoder_1 (
    .out1(decoder_1_out1), .out2(decoder_1_out2), .out3(decoder_1_out3), .out4(decoder_1_out4),
    .out5(decoder_1_out5), .out6(decoder_1_out6), .out7(decoder_1_out7), .out8(decoder_1_out8),
    .out9(decoder_1_out9), .out11(decoder_1_out11), .out12(decoder_1_out11), .out13(decoder_1_out11),
    .out14(decoder_1_out11), .out15(decoder_1_out11), .sel({MSB, i, i2, LSB}), .en(1'b1));  // open: out0, out10
  or or_1 (or_1_out, decoder_1_out9, decoder_1_out8, decoder_1_out7, decoder_1_out6, decoder_1_out5);
  D_Flip_Flop d_ff_1 (.D(or_1_out), .clk(clk), .Q(OMSB), .reset(rst));  // open: Qn, preset
  or or_2 (or_2_out, decoder_1_out9, decoder_1_out4);
  D_Flip_Flop d_ff_2 (.D(or_2_out), .clk(clk), .Q(O), .reset(rst));  // open: Qn, preset
  D_Flip_Flop d_ff_3 (.D(or_3_out), .clk(clk), .Q(O1), .reset(rst));  // open: Qn, preset
  or or_3 (or_3_out, decoder_1_out8, decoder_1_out7, decoder_1_out3, decoder_1_out2);
  or or_4 (or_4_out, decoder_1_out8, decoder_1_out6, decoder_1_out3, decoder_1_out1);
  D_Flip_Flop d_ff_4 (.D(or_4_out), .clk(clk), .Q(OLSB), .reset(rst));  // open: Qn, preset
endmodule
