// Logisim project SPM8_8.circ as structural Verilog: 1 circuit, main circuit SPM
module SPM (
  input  x7,
  input  x6,
  input  x5,
  input  x4,
  input  x3,
  input  x2,
  input  x1,
  input  x0,
  input  y,
  input  R,
  output Prod,
  output done
);

  wire and_1_out, and_2_out, and_3_out, and_4_out, and_5_out, and_6_out, and_7_out, and_8_out, clk_out,
       csa_1_pp, csa_2_pp, csa_3_pp, csa_4_pp, csa_5_pp, csa_6_pp, tcmp_1_s;
  wire [7:0] bit_extender_1_out;

  Clock clk (.out(clk_out));
  and and_1 (and_1_out, y, x7);
  and and_2 (and_2_out, y, x6);
  and and_3 (and_3_out, y, x5);
  TCMP tcmp_1 (.A(and_1_out), .clk(clk_out), .rst(R), .S(tcmp_1_s));
  and and_4 (and_4_out, y, x4);
  and and_5 (and_5_out, y, x3);
  CSA csa_1 (.x(and_2_out), .y(tcmp_1_s), .R(R), .clk(clk_out), .pp(csa_1_pp));
  and and_6 (and_6_out, y, x2);
  and and_7 (and_7_out, y, x1);
  CSA csa_2 (.x(and_3_out), .y(csa_1_pp), .R(R), .clk(clk_out), .pp(csa_2_pp));
  and and_8 (and_8_out, y, x0);
  CSA csa_3 (.x(and_4_out), .y(csa_2_pp), .R(R), .clk(clk_out), .pp(csa_3_pp));
  CSA csa_4 (.x(and_5_out), .y(csa_3_pp), .R(R), .clk(clk_out), .pp(csa_4_pp));
  assign bit_extender_1_out = {{7{R}}, R};  // Bit_Extender bit_extender_1
  CSA csa_5 (.x(and_6_out), .y(csa_4_pp), .R(R), .clk(clk_out), .pp(csa_5_pp));
  Counter #(.max('h10)) counter_1 (
    .clr(R), .load(1'b0), .up(1'b1), .count(1'b1), .clk(clk_out), .D(bit_extender_1_out), .carry(done));  // open: Q
  CSA csa_6 (.x(and_7_out), .y(csa_5_pp), .R(R), .clk(clk_out), .pp(csa_6_pp));
  CSA csa_7 (.x(and_8_out), .y(csa_6_pp), .R(R), .clk(clk_out), .pp(Prod));
endmodule
