// Logisim project TCMP.circ as structural Verilog: 1 circuit, main circuit TCMP
module TCMP (
  input  A,
  input  clk,
  input  rst,
  output S
);

  wire d_ff_2_q, or_1_out, xor_1_out;

  or or_1 (or_1_out, d_ff_2_q, A);
  xor xor_1 (xor_1_out, A, d_ff_2_q);
  D_Flip_Flop d_ff_1 (.D(xor_1_out), .clk(clk), .Q(S), .reset(rst));  // open: Qn, preset
  D_Flip_Flop d_ff_2 (.D(or_1_out), .clk(clk), .Q(d_ff_2_q), .reset(rst));  // open: Qn, preset
endmodule
