// Logisim project carry_save_adder.circ as structural Verilog: 1 circuit, main circuit CSA
module CSA (
  input  x,
  input  y,
  input  R,
  output pp
);

  wire adder_1_cout, and_1_out, and_2_out, clock_1_out, d_ff_2_p1, xor_1_out;
  wire [7:0] adder_1_out, d_ff_2_p4;
  wire [7:1] undriven;

  xor xor_1 (xor_1_out, x, adder_1_out[0]);
  Clock clock_1 (.out(clock_1_out));
  and and_1 (and_1_out, x, adder_1_out[0]);
  D_Flip_Flop d_ff_1 (.D(xor_1_out), .clk(clock_1_out), .Q(pp), .reset(R));  // open: Qn, preset
  Adder adder_1 (.a({undriven, y}), .b(d_ff_2_p4), .out(adder_1_out), .cin(1'b0), .cout(adder_1_cout));
  and and_2 (and_2_out, and_1_out, adder_1_cout);
  // D_Flip_Flop d_ff_2: pin names not known; wires that end beside it: d_ff_2_p1, clock_1_out, R, d_ff_2_p4, and_2_out
  xor xor_2 (d_ff_2_p1, and_1_out, adder_1_cout);
  // Pins of 1 and 8 bits meet at {undriven, y}
  // Pins of 1 and 8 bits meet at adder_1_out

  // Notes on the sheet:
  //   X
  //   Y
  //   Clk
endmodule
