// Logisim project control.circ as structural Verilog: 1 circuit, main circuit controlcirc
module controlcirc (
  input  BTNC,
  input  clk,
  input  [7:0] y,
  input  en,
  input  [7:0] x,
  input  done,
  output yout,
  output x0,
  output x1,
  output x2,
  output x3,
  output LD0,
  output x4,
  output x5,
  output x6,
  output x7
);

  wire and_1_out, or_1_out;

  // Shift_Register shift_register_1: pin names not known; wires that end beside it: 1'b0, BTNC, clk, clk, y[7], y[7], y[6], y[5], y[4], y[3], y[2], y[1], y[0], yout
  or or_1 (or_1_out, done, LD0);
  and and_1 (and_1_out, en, or_1_out);
  D_Flip_Flop d_ff_1 (.D(and_1_out), .clk(clk), .Q(LD0));  // open: Qn, preset, reset

  assign x0 = x[0];
  assign x1 = x[1];
  assign x2 = x[2];
  assign x3 = x[3];
  assign x4 = x[4];
  assign x5 = x[5];
  assign x6 = x[6];
  assign x7 = x[7];
endmodule
