// Logisim project maincirc.circ as structural Verilog: 2 circuits, main circuit main
module main (
  input  BTNC,
  input  [7:0] y,
  input  [7:0] x,
  input  rst
);

  wire clk_out, controlcirc_1_ld0, controlcirc_1_x0, controlcirc_1_x1, controlcirc_1_x2, controlcirc_1_x3,
       controlcirc_1_x4, controlcirc_1_x5, controlcirc_1_x6, controlcirc_1_x7, controlcirc_1_yout, not_1_out,
       spm_1_done, undriven, undriven_2, undriven_3, undriven_4, undriven_5, undriven_6, undriven_7;
  wire [3:0] dda_2_omsb, dda_3_omsb, dda_4_omsb, spm_1_prod;

  SPM spm_1 (
    .x7(controlcirc_1_x7), .x6(controlcirc_1_x6), .x5(controlcirc_1_x5), .x4(controlcirc_1_x4),
    .x3(controlcirc_1_x3), .x2(controlcirc_1_x2), .x1(controlcirc_1_x1), .x0(controlcirc_1_x0),
    .y(controlcirc_1_yout), .R(rst), .Prod(spm_1_prod[0]), .done(spm_1_done));
  not not_1 (not_1_out, rst);
  _7_Segment_Display u_7_segment_display_1 ();  // open: g, f, a, b, e, d, c, dp
  DDA dda_1 (
    .MSB(dda_2_omsb[3]), .clk(clk_out), .rst(rst), .i(dda_2_omsb[2]), .i2(dda_2_omsb[1]),
    .LSB(dda_2_omsb[0]), .O(dda_2_omsb[3]), .O1(dda_2_omsb[2]), .OLSB(dda_2_omsb[1]));  // open: OMSB
  _7_Segment_Display u_7_segment_display_2 ();  // open: g, f, a, b, e, d, c, dp
  DDA dda_2 (
    .MSB(dda_3_omsb[3]), .clk(clk_out), .rst(rst), .i(dda_3_omsb[2]), .i2(dda_3_omsb[1]),
    .LSB(dda_3_omsb[0]), .OMSB(dda_2_omsb[0]), .O(dda_3_omsb[3]), .O1(dda_3_omsb[2]), .OLSB(dda_3_omsb[1]));
  Clock clk (.out(clk_out));
  _7_Segment_Display u_7_segment_display_3 ();  // open: g, f, a, b, e, d, c, dp
  DDA dda_3 (
    .MSB(dda_4_omsb[3]), .clk(clk_out), .rst(rst), .i(dda_4_omsb[2]), .i2(dda_4_omsb[1]),
    .LSB(dda_4_omsb[0]), .OMSB(dda_3_omsb[0]), .O(dda_4_omsb[3]), .O1(dda_4_omsb[2]), .OLSB(dda_4_omsb[1]));
  _7_Segment_Display u_7_segment_display_4 (
    .g(undriven), .f(undriven_4), .a(undriven_5), .b(undriven_7), .e(undriven_2), .d(undriven_3),
    .c(undriven_6));  // open: dp
  controlcirc controlcirc_1 (
    .BTNC(BTNC), .clk(clk_out), .y(y), .en(not_1_out), .x(x), .done(spm_1_done), .yout(controlcirc_1_yout),
    .x0(controlcirc_1_x0), .x1(controlcirc_1_x1), .x2(controlcirc_1_x2), .x3(controlcirc_1_x3),
    .LD0(controlcirc_1_ld0), .x4(controlcirc_1_x4), .x5(controlcirc_1_x5), .x6(controlcirc_1_x6),
    .x7(controlcirc_1_x7));
  DDA dda_4 (
    .MSB(spm_1_prod[3]), .clk(clk_out), .rst(rst), .i(spm_1_prod[2]), .i2(spm_1_prod[1]),
    .LSB(spm_1_prod[0]), .OMSB(dda_4_omsb[0]), .O(spm_1_prod[3]), .O1(spm_1_prod[2]), .OLSB(spm_1_prod[1]));
  LED LD0 (.in(controlcirc_1_ld0));
endmodule

module cintoBCD (
  input  [3:0] i,
  output Fo,
  output Ao,
  output Go,
  output Bo,
  output Co,
  output Do,
  output Eo
);

  wire decoder_1_out0, decoder_1_out1, decoder_1_out2, decoder_1_out3, decoder_1_out4, decoder_1_out5,
       decoder_1_out6, decoder_1_out7, decoder_1_out8, decoder_1_out9;

  Decoder #(.select(4)) decoder_1 (
    .out0(decoder_1_out0), .out1(decoder_1_out1), .out2(decoder_1_out2), .out3(decoder_1_out3),
    .out4(decoder_1_out4), .out5(decoder_1_out5), .out6(decoder_1_out6), .out7(decoder_1_out7),
    .out8(decoder_1_out8), .out9(decoder_1_out9), .sel(i), .en(1'b1));  // open: out10, out11, out12, out13, out14, out15
  or A (Ao, decoder_1_out0, decoder_1_out2, decoder_1_out3, decoder_1_out5, decoder_1_out6, decoder_1_out7, decoder_1_out8, decoder_1_out9);
  or B (Bo, decoder_1_out0, decoder_1_out1, decoder_1_out2, decoder_1_out3, decoder_1_out4, decoder_1_out7, decoder_1_out8, decoder_1_out9);
  or C (Co, decoder_1_out0, decoder_1_out1, decoder_1_out3, decoder_1_out4, decoder_1_out5, decoder_1_out6, decoder_1_out7, decoder_1_out8, decoder_1_out9);
  or D (Do, decoder_1_out0, decoder_1_out2, decoder_1_out3, decoder_1_out5, decoder_1_out6, decoder_1_out8, decoder_1_out9);
  or E (Eo, decoder_1_out0, decoder_1_out2, decoder_1_out6, decoder_1_out8);
  or F (Fo, decoder_1_out0, decoder_1_out4, decoder_1_out5, decoder_1_out6, decoder_1_out8, decoder_1_out9);
  or G (Go, decoder_1_out2, decoder_1_out3, decoder_1_out4, decoder_1_out5, decoder_1_out6, decoder_1_out8, decoder_1_out9);
endmodule
