// Logisim project carry_save_adder.circ as structural Verilog: 1 circuit, main circuit main
module main (
  input  in_1,
  input  Y,
  input  R
);

  wire adder_1_cout, and_1_out, clock_1_out, d_ff_1_q, undriven_2, xor_1_out, xor_2_out;
  wire [7:0] adder_1_out, d_ff_2_q;
  wire [7:1] undriven;

  xor xor_1 (xor_1_out, in_1, adder_1_out[0]);
  Clock clock_1 (.out(clock_1_out));
  and and_1 (and_1_out, in_1, adder_1_out[0]);
  D_Flip_Flop d_ff_1 (.D(xor_1_out), .clk(clock_1_out), .Q(d_ff_1_q), .reset(undriven_2));  // open: Qn, preset
  Adder adder_1 (.a({undriven, Y}), .b(d_ff_2_q), .out(adder_1_out), .cin(1'b0), .cout(adder_1_cout));
  // AND_Gate and_2 has open pins: in0=and_1_out, in1=adder_1_cout, out=open
  D_Flip_Flop d_ff_2 (.D(xor_2_out), .clk(clock_1_out), .Q(d_ff_2_q[0]), .reset(R));  // open: Qn, preset
  xor xor_2 (xor_2_out, and_1_out, adder_1_cout);
  // Pins of 1 and 8 bits meet at adder_1_out
  // Pins of 1 and 8 bits meet at {undriven, Y}
  // Pins of 1 and 8 bits meet at d_ff_2_q

  // Notes on the sheet:
  //   X
  //   Clk
endmodule
